// Logisim project RAMses.circ as structural Verilog
module main (
);

  wire CLOCK, clock_1_out, CONTINUE, d_ff_1_q, decoder_1_out0, decoder_1_out1, decoder_1_out2,
       \gerador_de_temporização_16_1_t0 , \gerador_de_temporização_16_1_t1 ,
       \gerador_de_temporização_16_1_t2 , \gerador_de_temporização_16_1_t3 ,
       \gerador_de_temporização_16_1_t4 , \gerador_de_temporização_16_1_t5 ,
       \gerador_de_temporização_16_1_t6 , \gerador_de_temporização_16_1_t7 ,
       \gerador_de_temporização_16_1_t8 , \gerador_de_temporização_16_1_t9 , INC_PC, ON, or_1_out, RESET, RM,
       W_PC, W_RDM, W_REG_COND, W_REM, W_RI, WM;
  wire [1:0] MUX_PC, MUX_RDM, MUX_REM, MUX_X, W_REG;
  wire [2:0] register_1_q, ULA, unidade_logica_aritimetica_8bits_1_zero;
  wire [7:0] adder_1_out, adder_2_out, multiplexer_1_out, multiplexer_2_out, multiplexer_3_out,
       multiplexer_4_out, PC, RA, ram_1_data, RB_q, RDM_q, REM_q, RI_q, RX_q,
       unidade_logica_aritimetica_8bits_1_saida;
  wire [8:0] mux_3diplay_7seg_1_out_3, mux_3diplay_7seg_2_out_3;
  wire [11:0] mux_3diplay_7seg_1_out_2, mux_3diplay_7seg_2_out_2;

  Decoder #(.select(2)) decoder_1 (
    .out0(decoder_1_out0), .out1(decoder_1_out1), .out2(decoder_1_out2), .sel(W_REG));  // open: out3, en
  Register RX (.D(unidade_logica_aritimetica_8bits_1_saida), .en(decoder_1_out2), .Q(RX_q), .clk(CLOCK), .clr(RESET));
  Register u_RA (.D(unidade_logica_aritimetica_8bits_1_saida), .en(decoder_1_out0), .Q(RA), .clk(CLOCK), .clr(RESET));
  Register RB (.D(unidade_logica_aritimetica_8bits_1_saida), .en(decoder_1_out1), .Q(RB_q), .clk(CLOCK), .clr(RESET));
  // Probe on RA
  // Probe on multiplexer_1_out
  // Probe on unidade_logica_aritimetica_8bits_1_saida
  Button u_Reset (.out(RESET));
  Multiplexer #(.select(2), .width(8)) multiplexer_1 (
    .in0(RA), .in1(RB_q), .in2(RX_q), .in3({8{1'b0}}), .out(multiplexer_1_out), .sel(MUX_X));  // open: en
  // Probe on ULA
  and and_1 (CLOCK, ON, clock_1_out);
  Clock clock_1 (.out(clock_1_out));
  Unidade_Logica_Aritimetica_8bits unidade_logica_aritimetica_8bits_1 (
    .A(multiplexer_1_out), .B(RDM_q), .\Funçao (ULA), .Negativo(unidade_logica_aritimetica_8bits_1_zero[1]),
    .Vai_Um(unidade_logica_aritimetica_8bits_1_zero[2]), .ZERO(unidade_logica_aritimetica_8bits_1_zero[0]),
    .Saida(unidade_logica_aritimetica_8bits_1_saida));
  // Probe on adder_1_out
  Adder adder_1 (.a(RX_q), .b(RDM_q), .out(adder_1_out));  // open: cin, cout
  // Probe on MUX_PC
  // Probe on RDM_q
  D_Flip_Flop #(.trigger("falling")) d_ff_1 (.clk(CLOCK), .D(CONTINUE), .Q(d_ff_1_q));  // open: Qn, preset, en, reset
  // Probe on multiplexer_2_out
  Multiplexer #(.select(2), .width(8)) multiplexer_2 (
    .in0(RDM_q), .in1(adder_1_out), .in2(REM_q), .in3(adder_2_out), .out(multiplexer_2_out), .sel(MUX_PC));  // open: en
  Register #(.width(3)) register_1 (
    .D(unidade_logica_aritimetica_8bits_1_zero), .en(W_REG_COND), .Q(register_1_q), .clk(CLOCK), .clr(RESET));
  \Gerador_de_Temporização___16  \gerador_de_temporização_16_1  (
    .Clock(CLOCK), .T0(\gerador_de_temporização_16_1_t0 ), .T1(\gerador_de_temporização_16_1_t1 ),
    .T2(\gerador_de_temporização_16_1_t2 ), .T3(\gerador_de_temporização_16_1_t3 ),
    .T4(\gerador_de_temporização_16_1_t4 ), .T5(\gerador_de_temporização_16_1_t5 ),
    .T6(\gerador_de_temporização_16_1_t6 ), .T7(\gerador_de_temporização_16_1_t7 ), .Limpar(or_1_out),
    .T8(\gerador_de_temporização_16_1_t8 ), .T9(\gerador_de_temporização_16_1_t9 ));  // open: T10, T11, T12, T13, T14, T15
  or or_1 (or_1_out, d_ff_1_q, RESET);
  Counter u_PC (.load(W_PC), .D(multiplexer_2_out), .count(INC_PC), .Q(PC), .clk(CLOCK), .clr(RESET));  // open: carry
  Register RI (.D(RDM_q), .en(W_RI), .Q(RI_q), .clk(CLOCK), .clr(RESET));
  Multiplexer #(.select(2), .width(8)) multiplexer_3 (
    .in0(PC), .in1(adder_1_out), .in2(RDM_q), .out(multiplexer_3_out), .sel(MUX_REM));  // open: in3, en
  Unidade_de_Controle unidade_de_controle_1 (
    .t0(\gerador_de_temporização_16_1_t0 ), .t1(\gerador_de_temporização_16_1_t1 ),
    .t2(\gerador_de_temporização_16_1_t2 ), .t3(\gerador_de_temporização_16_1_t3 ),
    .t4(\gerador_de_temporização_16_1_t4 ), .t5(\gerador_de_temporização_16_1_t5 ),
    .t6(\gerador_de_temporização_16_1_t6 ), .t7(\gerador_de_temporização_16_1_t7 ),
    .t8(\gerador_de_temporização_16_1_t8 ), .t9(\gerador_de_temporização_16_1_t9 ), .ESTADO(register_1_q),
    .\INSTRUÇÂO (RI_q), .W_REG(W_REG), .MUX_X(MUX_X), .ULA(ULA), .W_REG_CON(W_REG_COND), .MUX_PC(MUX_PC),
    .W_PC(W_PC), .MUX_REM(MUX_REM), .MUX_RDM(MUX_RDM), .W_RI(W_RI), .W_RDM(W_RDM), .W_REM(W_REM), .ON(ON),
    .INC_PC(INC_PC), .RM(RM), .WM(WM), .BREAK(CONTINUE));
  Register #(.trigger("falling")) REM (.D(multiplexer_3_out), .en(W_REM), .Q(REM_q), .clk(CLOCK), .clr(RESET));
  Adder adder_2 (.a(8'h1), .b(REM_q), .out(adder_2_out));  // open: cin, cout
  Multiplexer #(.select(2), .width(8)) multiplexer_4 (
    .in0(multiplexer_1_out), .in1(ram_1_data), .in2(PC), .out(multiplexer_4_out), .sel(MUX_RDM));  // open: in3, en
  Register RDM (.D(multiplexer_4_out), .en(W_RDM), .Q(RDM_q), .clk(CLOCK), .clr(RESET));
  RAM #(.bus("separate")) ram_1 (
    .addr(REM_q), .din(RDM_q), .data(ram_1_data), .str(WM), .clk(CLOCK), .ld(RM));  // open: sel, clr
  _7_Segment_Display u_7_segment_display_1 (
    .g(mux_3diplay_7seg_1_out_2[0]), .f(mux_3diplay_7seg_1_out_2[1]), .a(mux_3diplay_7seg_1_out_2[2]),
    .b(mux_3diplay_7seg_1_out_2[3]), .e(mux_3diplay_7seg_1_out_3[0]), .d(mux_3diplay_7seg_1_out_3[1]),
    .c(mux_3diplay_7seg_1_out_3[2]));  // open: dp
  MUX_3DIPLAY_7SEG mux_3diplay_7seg_1 (
    .Entrada(RA), .out_2(mux_3diplay_7seg_1_out_2), .out_3(mux_3diplay_7seg_1_out_3));
  _7_Segment_Display u_7_segment_display_2 (
    .g(mux_3diplay_7seg_2_out_2[0]), .f(mux_3diplay_7seg_2_out_2[1]), .a(mux_3diplay_7seg_2_out_2[2]),
    .b(mux_3diplay_7seg_2_out_2[3]), .e(mux_3diplay_7seg_2_out_3[0]), .d(mux_3diplay_7seg_2_out_3[1]),
    .c(mux_3diplay_7seg_2_out_3[2]));  // open: dp
  MUX_3DIPLAY_7SEG mux_3diplay_7seg_2 (
    .Entrada(PC), .out_2(mux_3diplay_7seg_2_out_2), .out_3(mux_3diplay_7seg_2_out_3));
  _7_Segment_Display u_7_segment_display_3 (
    .g(mux_3diplay_7seg_1_out_2[4]), .f(mux_3diplay_7seg_1_out_2[5]), .a(mux_3diplay_7seg_1_out_2[6]),
    .b(mux_3diplay_7seg_1_out_2[7]), .e(mux_3diplay_7seg_1_out_3[3]), .d(mux_3diplay_7seg_1_out_3[4]),
    .c(mux_3diplay_7seg_1_out_3[5]));  // open: dp
  _7_Segment_Display u_7_segment_display_4 (
    .g(mux_3diplay_7seg_1_out_2[8]), .f(mux_3diplay_7seg_1_out_2[9]), .a(mux_3diplay_7seg_1_out_2[10]),
    .b(mux_3diplay_7seg_1_out_2[11]), .e(mux_3diplay_7seg_1_out_3[6]), .d(mux_3diplay_7seg_1_out_3[7]),
    .c(mux_3diplay_7seg_1_out_3[8]));  // open: dp
  _7_Segment_Display u_7_segment_display_5 (
    .g(mux_3diplay_7seg_2_out_2[8]), .f(mux_3diplay_7seg_2_out_2[9]), .a(mux_3diplay_7seg_2_out_2[10]),
    .b(mux_3diplay_7seg_2_out_2[11]), .e(mux_3diplay_7seg_2_out_3[6]), .d(mux_3diplay_7seg_2_out_3[7]),
    .c(mux_3diplay_7seg_2_out_3[8]));  // open: dp
  _7_Segment_Display u_7_segment_display_6 (
    .g(mux_3diplay_7seg_2_out_2[4]), .f(mux_3diplay_7seg_2_out_2[5]), .a(mux_3diplay_7seg_2_out_2[6]),
    .b(mux_3diplay_7seg_2_out_2[7]), .e(mux_3diplay_7seg_2_out_3[3]), .d(mux_3diplay_7seg_2_out_3[4]),
    .c(mux_3diplay_7seg_2_out_3[5]));  // open: dp

  // Notes on the sheet:
  //   Pc
  //   REM
  //   RDM
endmodule

module deslocador (
  input  D1,
  input  D2,
  input  D3,
  input  D4,
  input  D5,
  input  D6,
  input  D7,
  input  D8,
  input  C,
  output out_10,
  output out_11,
  output out_12,
  output out_13,
  output out_14,
  output out_15,
  output out_16,
  output out_17
);

  wire and_1_out, and_3_out, and_4_out, and_5_out, and_6_out, and_7_out, and_8_out, and_9_out, and_10_out,
       and_11_out, and_12_out, and_14_out, not_1_out;

  and and_1 (and_1_out, D1, C);
  not not_1 (not_1_out, C);
  and and_2 (out_10, not_1_out, D2);
  and and_3 (and_3_out, D2, C);
  or or_1 (out_11, and_1_out, and_4_out);
  and and_4 (and_4_out, not_1_out, D3);
  or or_2 (out_12, and_3_out, and_6_out);
  and and_5 (and_5_out, D3, C);
  and and_6 (and_6_out, not_1_out, D4);
  and and_7 (and_7_out, D4, C);
  or or_3 (out_13, and_5_out, and_8_out);
  and and_8 (and_8_out, not_1_out, D5);
  and and_9 (and_9_out, D5, C);
  or or_4 (out_14, and_7_out, and_10_out);
  and and_10 (and_10_out, not_1_out, D6);
  and and_11 (and_11_out, D6, C);
  or or_5 (out_15, and_9_out, and_12_out);
  and and_12 (and_12_out, not_1_out, D7);
  or or_6 (out_16, and_11_out, and_14_out);
  and and_13 (out_17, D7, C);
  and and_14 (and_14_out, not_1_out, D8);
endmodule

// ULA(M)
module Unidade_Logica_Aritimetica_meio (
  input  A__inverter,
  input  A__habilitar,
  input  A,
  input  B,
  input  B__habilitar,
  input  F0,
  input  F1,
  input  F2,
  output Saida,
  output Vai_um
);

  wire and_1_out, and_2_out, and_3_out, complemento_de_2_completo_1_saida,
       complemento_de_2_completo_1_vai_um, decodificador3bits_1_d0, decodificador3bits_1_d1,
       decodificador3bits_1_d2, decodificador3bits_1_d3, decodificador3bits_1_d4, decodificador3bits_1_d5,
       decodificador3bits_1_d6, decodificador3bits_1_d7, deslocador_completo_1_saida,
       deslocador_completo_1_vai_um, somador_completo_1_resultado, somador_completo_1_vai_um,
       subtrador_completo_1_saida, subtrador_completo_1_vai_um, unidade_logica_1_and__saida,
       unidade_logica_1_not__saida, unidade_logica_1_or__saida, xor_1_out;

  and and_1 (and_1_out, A__habilitar, A);
  and and_2 (and_2_out, B, B__habilitar);
  Decodificador3Bits decodificador3bits_1 (
    .F0(F0), .F1(F1), .F2(F2), .D0(decodificador3bits_1_d0), .D1(decodificador3bits_1_d1),
    .D2(decodificador3bits_1_d2), .D3(decodificador3bits_1_d3), .D4(decodificador3bits_1_d4),
    .D5(decodificador3bits_1_d5), .D6(decodificador3bits_1_d6), .D7(decodificador3bits_1_d7));
  xor xor_1 (xor_1_out, A__inverter, and_1_out);
  and and_3 (and_3_out, and_2_out, decodificador3bits_1_d7);
  Unidade_Logica unidade_logica_1 (
    .A(xor_1_out), .B(and_2_out), .AND__habilita(decodificador3bits_1_d2),
    .OR__habilita(decodificador3bits_1_d3), .NOT__habilita(decodificador3bits_1_d4),
    .AND__saida(unidade_logica_1_and__saida), .OR__saida(unidade_logica_1_or__saida),
    .NOT__saida(unidade_logica_1_not__saida));
  Somador_Completo somador_completo_1 (
    .A(xor_1_out), .B(and_2_out), .Habilitar(decodificador3bits_1_d0), .Vem_um(1'b0),
    .Vai_Um(somador_completo_1_vai_um), .Resultado(somador_completo_1_resultado));
  Subtrador_Completo subtrador_completo_1 (
    .A(xor_1_out), .B(and_2_out), .Habilitar(decodificador3bits_1_d1), .Vem_um(1'b0),
    .Vai_um(subtrador_completo_1_vai_um), .Saida(subtrador_completo_1_saida));
  ExactlyOne xor_2 (
    .out(Vai_um), .in0(somador_completo_1_vai_um), .in1(subtrador_completo_1_vai_um),
    .in2(complemento_de_2_completo_1_vai_um), .in3(deslocador_completo_1_vai_um));
  Complemento_de_2_Completo complemento_de_2_completo_1 (
    .A(xor_1_out), .Vem_um(1'b1), .Habilitar(decodificador3bits_1_d5),
    .Vai_um(complemento_de_2_completo_1_vai_um), .Saida(complemento_de_2_completo_1_saida));
  Deslocador_Completo deslocador_completo_1 (
    .A(xor_1_out), .Vem_um(1'b0), .Habilitar(decodificador3bits_1_d6), .Vai_um(deslocador_completo_1_vai_um),
    .Saida(deslocador_completo_1_saida));
  ExactlyOne xor_3 (
    .out(Saida), .in0(unidade_logica_1_and__saida), .in1(unidade_logica_1_or__saida),
    .in2(unidade_logica_1_not__saida), .in3(and_3_out), .in4(somador_completo_1_resultado),
    .in5(subtrador_completo_1_saida), .in6(complemento_de_2_completo_1_saida),
    .in7(deslocador_completo_1_saida));
endmodule

// ULA
module Unidade_Logica_Aritimetica_Completo (
  input  Vem_um,
  input  A__inverter,
  input  A__habilitar,
  input  A,
  input  B,
  input  B__habilitar,
  input  F0,
  input  F1,
  input  F2,
  output Saida,
  output Vai_um
);

  wire and_1_out, and_2_out, and_3_out, complemento_de_2_completo_1_saida,
       complemento_de_2_completo_1_vai_um, decodificador3bits_1_d0, decodificador3bits_1_d1,
       decodificador3bits_1_d2, decodificador3bits_1_d3, decodificador3bits_1_d4, decodificador3bits_1_d5,
       decodificador3bits_1_d6, decodificador3bits_1_d7, deslocador_completo_1_saida,
       deslocador_completo_1_vai_um, somador_completo_1_resultado, somador_completo_1_vai_um,
       subtrador_completo_1_saida, subtrador_completo_1_vai_um, unidade_logica_1_and__saida,
       unidade_logica_1_not__saida, unidade_logica_1_or__saida, xor_1_out;

  and and_1 (and_1_out, A__habilitar, A);
  and and_2 (and_2_out, B, B__habilitar);
  Decodificador3Bits decodificador3bits_1 (
    .F0(F0), .F1(F1), .F2(F2), .D0(decodificador3bits_1_d0), .D1(decodificador3bits_1_d1),
    .D2(decodificador3bits_1_d2), .D3(decodificador3bits_1_d3), .D4(decodificador3bits_1_d4),
    .D5(decodificador3bits_1_d5), .D6(decodificador3bits_1_d6), .D7(decodificador3bits_1_d7));
  xor xor_1 (xor_1_out, A__inverter, and_1_out);
  and and_3 (and_3_out, and_2_out, decodificador3bits_1_d7);
  Unidade_Logica unidade_logica_1 (
    .A(xor_1_out), .B(and_2_out), .AND__habilita(decodificador3bits_1_d2),
    .OR__habilita(decodificador3bits_1_d3), .NOT__habilita(decodificador3bits_1_d4),
    .AND__saida(unidade_logica_1_and__saida), .OR__saida(unidade_logica_1_or__saida),
    .NOT__saida(unidade_logica_1_not__saida));
  Somador_Completo somador_completo_1 (
    .A(xor_1_out), .B(and_2_out), .Habilitar(decodificador3bits_1_d0), .Vem_um(Vem_um),
    .Vai_Um(somador_completo_1_vai_um), .Resultado(somador_completo_1_resultado));
  Subtrador_Completo subtrador_completo_1 (
    .A(xor_1_out), .B(and_2_out), .Habilitar(decodificador3bits_1_d1), .Vem_um(Vem_um),
    .Vai_um(subtrador_completo_1_vai_um), .Saida(subtrador_completo_1_saida));
  ExactlyOne xor_2 (
    .out(Vai_um), .in0(somador_completo_1_vai_um), .in1(subtrador_completo_1_vai_um),
    .in2(complemento_de_2_completo_1_vai_um), .in3(deslocador_completo_1_vai_um));
  Complemento_de_2_Completo complemento_de_2_completo_1 (
    .A(xor_1_out), .Vem_um(Vem_um), .Habilitar(decodificador3bits_1_d5),
    .Vai_um(complemento_de_2_completo_1_vai_um), .Saida(complemento_de_2_completo_1_saida));
  Deslocador_Completo deslocador_completo_1 (
    .A(xor_1_out), .Vem_um(Vem_um), .Habilitar(decodificador3bits_1_d6),
    .Vai_um(deslocador_completo_1_vai_um), .Saida(deslocador_completo_1_saida));
  ExactlyOne xor_3 (
    .out(Saida), .in0(unidade_logica_1_and__saida), .in1(unidade_logica_1_or__saida),
    .in2(unidade_logica_1_not__saida), .in3(and_3_out), .in4(somador_completo_1_resultado),
    .in5(subtrador_completo_1_saida), .in6(complemento_de_2_completo_1_saida),
    .in7(deslocador_completo_1_saida));
endmodule

// ULA 8
module Unidade_Logica_Aritimetica_8bits (
  input  [7:0] A,
  input  [7:0] B,
  input  [2:0] \Funçao ,
  output [7:0] Saida,
  output ZERO,
  output Negativo,
  output Vai_Um
);

  wire not_1_out, unidade_logica_aritimetica_completo_1_vai_um, unidade_logica_aritimetica_completo_2_vai_um,
       unidade_logica_aritimetica_completo_3_vai_um, unidade_logica_aritimetica_completo_4_vai_um,
       unidade_logica_aritimetica_completo_5_vai_um, unidade_logica_aritimetica_completo_6_vai_um,
       unidade_logica_aritimetica_meio_1_vai_um;
  wire [1:1] and_1_out;
  wire [6:0] unidade_logica_aritimetica_meio_1_saida;

  not not_1 (not_1_out, \Funçao [0]);
  and and_1 (and_1_out[1], \Funçao [1], not_1_out, \Funçao [2]);
  Unidade_Logica_Aritimetica_meio unidade_logica_aritimetica_meio_1 (
    .A__inverter(1'b0), .A__habilitar(1'b1), .A(A[0]), .B(B[0]), .B__habilitar(1'b1), .F0(\Funçao [0]),
    .F1(\Funçao [1]), .F2(\Funçao [2]), .Vai_um(unidade_logica_aritimetica_meio_1_vai_um),
    .Saida(unidade_logica_aritimetica_meio_1_saida[0]));
  Unidade_Logica_Aritimetica_Completo unidade_logica_aritimetica_completo_1 (
    .A__inverter(1'b0), .A__habilitar(1'b1), .A(A[1]), .B(B[1]), .B__habilitar(1'b1), .F0(\Funçao [0]),
    .F1(\Funçao [1]), .F2(\Funçao [2]), .Vem_um(unidade_logica_aritimetica_meio_1_vai_um),
    .Vai_um(unidade_logica_aritimetica_completo_1_vai_um), .Saida(unidade_logica_aritimetica_meio_1_saida[1]));
  Unidade_Logica_Aritimetica_Completo unidade_logica_aritimetica_completo_2 (
    .A__inverter(1'b0), .A__habilitar(1'b1), .A(A[2]), .B(B[2]), .B__habilitar(1'b1), .F0(\Funçao [0]),
    .F1(\Funçao [1]), .F2(\Funçao [2]), .Vem_um(unidade_logica_aritimetica_completo_1_vai_um),
    .Vai_um(unidade_logica_aritimetica_completo_2_vai_um), .Saida(unidade_logica_aritimetica_meio_1_saida[2]));
  Unidade_Logica_Aritimetica_Completo unidade_logica_aritimetica_completo_3 (
    .A__inverter(1'b0), .A__habilitar(1'b1), .A(A[3]), .B(B[3]), .B__habilitar(1'b1), .F0(\Funçao [0]),
    .F1(\Funçao [1]), .F2(\Funçao [2]), .Vem_um(unidade_logica_aritimetica_completo_2_vai_um),
    .Vai_um(unidade_logica_aritimetica_completo_3_vai_um), .Saida(unidade_logica_aritimetica_meio_1_saida[3]));
  Unidade_Logica_Aritimetica_Completo unidade_logica_aritimetica_completo_4 (
    .A__inverter(1'b0), .A__habilitar(1'b1), .A(A[4]), .B(B[4]), .B__habilitar(1'b1), .F0(\Funçao [0]),
    .F1(\Funçao [1]), .F2(\Funçao [2]), .Vem_um(unidade_logica_aritimetica_completo_3_vai_um),
    .Vai_um(unidade_logica_aritimetica_completo_4_vai_um), .Saida(unidade_logica_aritimetica_meio_1_saida[4]));
  Unidade_Logica_Aritimetica_Completo unidade_logica_aritimetica_completo_5 (
    .A__inverter(1'b0), .A__habilitar(1'b1), .A(A[5]), .B(B[5]), .B__habilitar(1'b1), .F0(\Funçao [0]),
    .F1(\Funçao [1]), .F2(\Funçao [2]), .Vem_um(unidade_logica_aritimetica_completo_4_vai_um),
    .Vai_um(unidade_logica_aritimetica_completo_5_vai_um), .Saida(unidade_logica_aritimetica_meio_1_saida[5]));
  Unidade_Logica_Aritimetica_Completo unidade_logica_aritimetica_completo_6 (
    .A__inverter(1'b0), .A__habilitar(1'b1), .A(A[6]), .B(B[6]), .B__habilitar(1'b1), .F0(\Funçao [0]),
    .F1(\Funçao [1]), .F2(\Funçao [2]), .Vem_um(unidade_logica_aritimetica_completo_5_vai_um),
    .Vai_um(unidade_logica_aritimetica_completo_6_vai_um), .Saida(unidade_logica_aritimetica_meio_1_saida[6]));
  Unidade_Logica_Aritimetica_Completo unidade_logica_aritimetica_completo_7 (
    .A__inverter(1'b0), .A__habilitar(1'b1), .A(A[7]), .B(B[7]), .B__habilitar(1'b1), .F0(\Funçao [0]),
    .F1(\Funçao [1]), .F2(\Funçao [2]), .Vem_um(unidade_logica_aritimetica_completo_6_vai_um),
    .Vai_um(Vai_Um), .Saida(Negativo));
  IsZero ISZERO (
    .in_1({Negativo, unidade_logica_aritimetica_meio_1_saida}),
    .\Saida___1_se_a_entrada_é_zero__0_caso_contrario (ZERO));
  Shifter #(.shift("lr")) shifter_1 (
    .in({Negativo, unidade_logica_aritimetica_meio_1_saida}), .\dist ({1'b0, and_1_out[1], 1'b0}), .out(Saida));
endmodule

// UL
module Unidade_Logica (
  input  A,
  input  B,
  input  AND__habilita,
  input  OR__habilita,
  input  NOT__habilita,
  output AND__saida,
  output OR__saida,
  output NOT__saida
);

  wire and_1_out, not_1_out, or_1_out;

  and and_1 (and_1_out, A, B);
  or or_1 (or_1_out, A, B);
  not not_1 (not_1_out, A);
  and and_2 (AND__saida, and_1_out, AND__habilita);
  and and_3 (OR__saida, or_1_out, OR__habilita);
  and and_4 (NOT__saida, not_1_out, NOT__habilita);
endmodule

// SUNCOM
module Somador_Completo (
  input  Vem_um,
  input  A,
  input  B,
  input  Habilitar,
  output Resultado,
  output Vai_Um
);

  wire and_1_out, and_2_out, xor_1_out, xor_2_out;

  and and_1 (and_1_out, Habilitar, B, A);
  xor xor_1 (xor_1_out, A, B);
  or or_1 (Vai_Um, and_1_out, and_2_out);
  and and_2 (and_2_out, Habilitar, xor_1_out, Vem_um);
  xor xor_2 (xor_2_out, Vem_um, xor_1_out);
  and and_3 (Resultado, xor_2_out, Habilitar);
endmodule

// SUBCOM
module Subtrador_Completo (
  input  Vem_um,
  input  A,
  input  B,
  input  Habilitar,
  output Saida,
  output Vai_um
);

  wire and_1_out, and_3_out, not_1_out, or_1_out, or_2_out, xor_1_out;

  not not_1 (not_1_out, A);
  and and_1 (and_1_out, not_1_out, or_1_out);
  and and_2 (Vai_um, Habilitar, or_2_out);
  or or_1 (or_1_out, B, Vem_um);
  or or_2 (or_2_out, and_1_out, and_3_out);
  xor xor_1 (xor_1_out, Vem_um, A, B);
  and and_3 (and_3_out, Vem_um, B, A);
  and and_4 (Saida, xor_1_out, Habilitar);
endmodule

// NEGCOM
module Complemento_de_2_Completo (
  input  Vem_um,
  input  A,
  input  Habilitar,
  output Saida,
  output Vai_um
);

  wire not_1_out, xor_1_out;

  not not_1 (not_1_out, A);
  and and_1 (Vai_um, not_1_out, Vem_um, Habilitar);
  xor xor_1 (xor_1_out, Vem_um, not_1_out);
  and and_2 (Saida, xor_1_out, Habilitar);
endmodule

// DESCOM
module Deslocador_Completo (
  input  Vem_um,
  input  A,
  input  Habilitar,
  output Saida,
  output Vai_um
);

  and and_1 (Vai_um, Habilitar, A);
  and and_2 (Saida, Vem_um, Habilitar);
endmodule

// DEC3B
module Decodificador3Bits (
  input  F0,
  input  F1,
  input  F2,
  output D0,
  output D1,
  output D2,
  output D3,
  output D4,
  output D5,
  output D6,
  output D7
);

  wire not_1_out, not_2_out, not_3_out, not_4_out, not_5_out, not_6_out, not_7_out, not_8_out, not_9_out,
       not_10_out, not_11_out, not_12_out;

  not not_1 (not_1_out, F0);
  not not_2 (not_2_out, F2);
  not not_3 (not_3_out, F1);
  not not_4 (not_4_out, F2);
  not not_5 (not_5_out, F1);
  not not_6 (not_6_out, F0);
  not not_7 (not_7_out, F2);
  not not_8 (not_8_out, F2);
  not not_9 (not_9_out, F1);
  not not_10 (not_10_out, F0);
  not not_11 (not_11_out, F1);
  not not_12 (not_12_out, F0);
  and and_1 (D0, not_1_out, not_2_out, not_3_out);
  and and_2 (D1, F0, not_4_out, not_5_out);
  and and_3 (D2, not_6_out, not_7_out, F1);
  and and_4 (D3, F1, not_8_out, F0);
  and and_5 (D4, not_9_out, F2, not_10_out);
  and and_6 (D5, not_11_out, F2, F0);
  and and_7 (D6, F1, F2, not_12_out);
  and and_8 (D7, F1, F2, F0);
endmodule

module ULA_in_8 (
  input  [7:0] A,
  input  [7:0] B,
  input  [2:0] Funcao
);

  wire [7:0] and_1_out;

  Decoder #(.select(3)) decoder_1 (.sel(Funcao), .en(1'b1));  // open: out0, out1, out2, out3, out4, out5, out6, out7
  assign and_1_out = A & B;  // AND_Gate and_1, 8 bits wide
endmodule

// FF-RSC
module flip_flop_R_S (
  input  Ativa,
  input  Reseta,
  output Saida
);

  wire nor_2_out;

  nor nor_1 (Saida, Reseta, nor_2_out);
  nor nor_2 (nor_2_out, Saida, Ativa);
endmodule

// REGISTRADOR
module registrador_8bits (
  input  [7:0] Entrada_de_Dados,
  input  Habilitar_Escrita,
  input  Resetar,
  input  Habilitar_Leitura,
  output [7:0] Saida
);

  wire and_1_out, and_2_out, and_4_out, and_6_out, and_8_out, and_10_out, and_12_out, and_14_out,
       flip_flop_r_s_1_saida, flip_flop_r_s_2_saida, flip_flop_r_s_3_saida, flip_flop_r_s_4_saida,
       flip_flop_r_s_5_saida, flip_flop_r_s_6_saida, flip_flop_r_s_7_saida, flip_flop_r_s_8_saida;

  and and_1 (and_1_out, Habilitar_Escrita, Entrada_de_Dados[7]);
  and and_2 (and_2_out, Habilitar_Escrita, Entrada_de_Dados[6]);
  flip_flop_R_S flip_flop_r_s_1 (.Ativa(and_1_out), .Reseta(Resetar), .Saida(flip_flop_r_s_1_saida));
  and and_3 (Saida[7], Habilitar_Leitura, flip_flop_r_s_1_saida);
  and and_4 (and_4_out, Habilitar_Escrita, Entrada_de_Dados[5]);
  flip_flop_R_S flip_flop_r_s_2 (.Ativa(and_2_out), .Reseta(Resetar), .Saida(flip_flop_r_s_2_saida));
  and and_5 (Saida[6], Habilitar_Leitura, flip_flop_r_s_2_saida);
  and and_6 (and_6_out, Habilitar_Escrita, Entrada_de_Dados[4]);
  flip_flop_R_S flip_flop_r_s_3 (.Ativa(and_4_out), .Reseta(Resetar), .Saida(flip_flop_r_s_3_saida));
  and and_7 (Saida[5], Habilitar_Leitura, flip_flop_r_s_3_saida);
  and and_8 (and_8_out, Habilitar_Escrita, Entrada_de_Dados[3]);
  flip_flop_R_S flip_flop_r_s_4 (.Ativa(and_6_out), .Reseta(Resetar), .Saida(flip_flop_r_s_4_saida));
  and and_9 (Saida[4], Habilitar_Leitura, flip_flop_r_s_4_saida);
  and and_10 (and_10_out, Habilitar_Escrita, Entrada_de_Dados[2]);
  flip_flop_R_S flip_flop_r_s_5 (.Ativa(and_8_out), .Reseta(Resetar), .Saida(flip_flop_r_s_5_saida));
  and and_11 (Saida[3], Habilitar_Leitura, flip_flop_r_s_5_saida);
  and and_12 (and_12_out, Habilitar_Escrita, Entrada_de_Dados[1]);
  flip_flop_R_S flip_flop_r_s_6 (.Ativa(and_10_out), .Reseta(Resetar), .Saida(flip_flop_r_s_6_saida));
  and and_13 (Saida[2], Habilitar_Leitura, flip_flop_r_s_6_saida);
  and and_14 (and_14_out, Habilitar_Escrita, Entrada_de_Dados[0]);
  flip_flop_R_S flip_flop_r_s_7 (.Ativa(and_12_out), .Reseta(Resetar), .Saida(flip_flop_r_s_7_saida));
  and and_15 (Saida[1], Habilitar_Leitura, flip_flop_r_s_7_saida);
  flip_flop_R_S flip_flop_r_s_8 (.Ativa(and_14_out), .Reseta(Resetar), .Saida(flip_flop_r_s_8_saida));
  and and_16 (Saida[0], Habilitar_Leitura, flip_flop_r_s_8_saida);
endmodule

module IsZero (
  input  [7:0] in_1,
  output \Saida___1_se_a_entrada_é_zero__0_caso_contrario 
);

  nor nor_1 (\Saida___1_se_a_entrada_é_zero__0_caso_contrario , in_1[0], in_1[1], in_1[2], in_1[3], in_1[4], in_1[5], in_1[6], in_1[7]);
endmodule

// GER-TEM
module \Gerador_de_Temporização___16  (
  input  Clock,
  input  Limpar,
  output T0,
  output T1,
  output T2,
  output T3,
  output T4,
  output T5,
  output T6,
  output T7,
  output T8,
  output T9,
  output T10,
  output T11,
  output T12,
  output T13,
  output T14,
  output T15
);

  wire [3:0] counter_1_q;

  Counter #(.width(4), .max('hf), .trigger("falling")) counter_1 (
    .Q(counter_1_q), .clk(Clock), .clr(Limpar));  // open: load, D, count, carry
  Decoder #(.select(4)) decoder_1 (
    .out0(T0), .out1(T1), .out2(T2), .out3(T3), .out4(T4), .out5(T5), .out6(T6), .out7(T7), .out8(T8),
    .out9(T9), .out10(T10), .out11(T11), .out12(T12), .out13(T13), .out14(T14), .out15(T15), .sel(counter_1_q));  // open: en
endmodule

// UC
module Unidade_de_Controle (
  input  [7:0] \INSTRUÇÂO ,
  input  [2:0] ESTADO,
  input  t0,
  input  t1,
  input  t2,
  input  t3,
  input  t4,
  input  t5,
  input  t6,
  input  t7,
  input  t8,
  input  t9,
  output [1:0] W_REG,
  output [1:0] MUX_X,
  output [2:0] ULA,
  output W_REG_CON,
  output [1:0] MUX_PC,
  output W_PC,
  output [1:0] MUX_REM,
  output [1:0] MUX_RDM,
  output W_RI,
  output W_RDM,
  output W_REM,
  output ON,
  output INC_PC,
  output RM,
  output WM,
  output BREAK
);

  wire and_1_out, and_2_out, and_3_out, and_4_out, and_5_out, and_6_out, and_7_out, and_8_out, and_9_out,
       and_10_out, and_11_out, and_12_out, and_13_out, and_14_out, and_15_out, and_16_out, and_17_out,
       and_18_out, comparator_1_eq, comparator_2_eq, comparator_3_eq, comparator_4_eq, comparator_5_eq,
       comparator_6_eq, comparator_7_eq, comparator_8_eq, comparator_9_eq, comparator_10_eq,
       comparator_11_eq, comparator_12_eq, comparator_13_eq, comparator_14_eq, comparator_15_eq,
       comparator_16_eq, comparator_17_eq, comparator_18_eq, comparator_19_eq, comparator_20_eq,
       comparator_21_eq, comparator_22_eq, ISJUMP, JUMP, nor_1_out, nor_2_out, nor_3_out, not_1_out,
       not_2_out, not_3_out, not_4_out, not_5_out, not_6_out, or_2_out, or_3_out, or_4_out, or_5_out,
       or_7_out;
  wire [20:0] controlled_buffer_2_out, controlled_buffer_3_out, controlled_buffer_4_out,
       controlled_buffer_5_out, controlled_buffer_6_out, controlled_buffer_7_out, controlled_buffer_8_out,
       controlled_buffer_9_out, controlled_buffer_10_out, controlled_buffer_11_out, controlled_buffer_12_out,
       controlled_buffer_14_out, controlled_buffer_15_out, controlled_buffer_16_out,
       controlled_buffer_17_out, controlled_buffer_18_out, controlled_buffer_19_out,
       controlled_buffer_20_out, controlled_buffer_21_out, controlled_buffer_22_out,
       controlled_buffer_23_out, controlled_buffer_24_out, controlled_buffer_25_out,
       controlled_buffer_26_out, controlled_buffer_27_out, controlled_buffer_28_out, EXECUTE,
       multiplexer_1_out, multiplexer_3_out, or_8_out, or_9_out, or_10_out, or_11_out, or_12_out,
       pull_resistor_2_node;
  wire [20:19] SAIDA;

  assign W_REG = SAIDA[20] ? \INSTRUÇÂO [3:2] : 2'bz;  // Controlled_Buffer controlled_buffer_1
  Comparator #(.width(4)) comparator_1 (.a(\INSTRUÇÂO [7:4]), .b(4'b1000), .eq(comparator_1_eq));  // open: gt, lt
  Comparator #(.width(4)) comparator_2 (.a(\INSTRUÇÂO [7:4]), .b(4'b1001), .eq(comparator_2_eq));  // open: gt, lt
  Comparator #(.width(4)) comparator_3 (.a(\INSTRUÇÂO [7:4]), .b(4'b1010), .eq(comparator_3_eq));  // open: gt, lt
  Comparator #(.width(4)) comparator_4 (.a(\INSTRUÇÂO [7:4]), .b(4'b1011), .eq(comparator_4_eq));  // open: gt, lt
  not not_1 (not_1_out, JUMP);
  Comparator #(.width(4), .mode("unsigned")) comparator_5 (
    .a(4'b0001), .b(\INSTRUÇÂO [7:4]), .eq(comparator_5_eq));  // open: gt, lt
  Comparator #(.width(4), .mode("unsigned")) comparator_6 (
    .a(\INSTRUÇÂO [7:4]), .b(4'b1100), .eq(comparator_6_eq));  // open: gt, lt
  Comparator #(.width(2), .mode("unsigned")) comparator_7 (
    .a(2'b10), .b(\INSTRUÇÂO [1:0]), .eq(comparator_7_eq));  // open: gt, lt
  Comparator #(.width(4), .mode("unsigned")) comparator_8 (
    .a(4'b0000), .b(\INSTRUÇÂO [7:4]), .eq(comparator_8_eq));  // open: gt, lt
  Comparator #(.width(4), .mode("unsigned")) comparator_9 (
    .a(4'b1111), .b(\INSTRUÇÂO [7:4]), .eq(comparator_9_eq));  // open: gt, lt
  Comparator #(.width(4), .mode("unsigned")) comparator_10 (
    .a(4'b1101), .b(\INSTRUÇÂO [7:4]), .eq(comparator_10_eq));  // open: gt, lt
  Comparator #(.width(4), .mode("unsigned")) comparator_11 (
    .a(4'b0110), .b(\INSTRUÇÂO [7:4]), .eq(comparator_11_eq));  // open: gt, lt
  Comparator #(.width(4), .mode("unsigned")) comparator_12 (
    .a(4'b1110), .b(\INSTRUÇÂO [7:4]), .eq(comparator_12_eq));  // open: gt, lt
  Comparator #(.width(2), .mode("unsigned")) comparator_13 (
    .a(2'b01), .b(\INSTRUÇÂO [1:0]), .eq(comparator_13_eq));  // open: gt, lt
  Comparator #(.width(2), .mode("unsigned")) comparator_14 (
    .a(2'b00), .b(\INSTRUÇÂO [1:0]), .eq(comparator_14_eq));  // open: gt, lt
  Comparator #(.width(2), .mode("unsigned")) comparator_15 (
    .a(2'b10), .b(\INSTRUÇÂO [1:0]), .eq(comparator_15_eq));  // open: gt, lt
  Comparator #(.width(2), .mode("unsigned")) comparator_16 (
    .a(2'b11), .b(\INSTRUÇÂO [1:0]), .eq(comparator_16_eq));  // open: gt, lt
  Comparator #(.width(2), .mode("unsigned")) comparator_17 (
    .a(2'b01), .b(\INSTRUÇÂO [1:0]), .eq(comparator_17_eq));  // open: gt, lt
  Comparator #(.width(4), .mode("unsigned")) comparator_18 (
    .a(4'b0001), .b(\INSTRUÇÂO [7:4]), .eq(comparator_18_eq));  // open: gt, lt
  Comparator #(.width(4), .mode("unsigned")) comparator_19 (
    .a(4'b1100), .b(\INSTRUÇÂO [7:4]), .eq(comparator_19_eq));  // open: gt, lt
  Comparator #(.width(2), .mode("unsigned")) comparator_20 (
    .a(2'b01), .b(\INSTRUÇÂO [1:0]), .eq(comparator_20_eq));  // open: gt, lt
  not not_2 (not_2_out, ISJUMP);
  Comparator #(.width(4), .mode("unsigned")) comparator_21 (
    .a(4'b0001), .b(\INSTRUÇÂO [7:4]), .eq(comparator_21_eq));  // open: gt, lt
  Comparator #(.width(4), .mode("unsigned")) comparator_22 (
    .a(4'b1100), .b(\INSTRUÇÂO [7:4]), .eq(comparator_22_eq));  // open: gt, lt
  assign controlled_buffer_2_out = t9 ? EXECUTE : 21'bz;  // Controlled_Buffer controlled_buffer_2
  or or_1 (ISJUMP, comparator_1_eq, comparator_2_eq, comparator_3_eq, comparator_4_eq);
  Multiplexer #(.select(2), .width(21)) multiplexer_1 (
    .in0(21'h71f11), .in1(21'h71f11), .in2(21'h76f19), .in3(21'h73f11), .out(multiplexer_1_out),
    .sel(\INSTRUÇÂO [1:0]));  // open: en
  and and_1 (and_1_out, not_1_out, ISJUMP);
  or or_2 (or_2_out, comparator_5_eq, comparator_6_eq, ISJUMP);
  and and_2 (and_2_out, comparator_14_eq, not_3_out);
  not not_3 (not_3_out, ISJUMP);
  and and_3 (and_3_out, comparator_14_eq, ISJUMP);
  assign controlled_buffer_3_out = and_4_out ? 21'h76730 : 21'bz;  // Controlled_Buffer controlled_buffer_3
  and and_4 (and_4_out, comparator_16_eq, not_4_out);
  not not_4 (not_4_out, ISJUMP);
  and and_5 (and_5_out, comparator_16_eq, ISJUMP);
  not not_5 (not_5_out, comparator_17_eq);
  nor nor_1 (nor_1_out, comparator_18_eq, comparator_19_eq);
  and and_6 (and_6_out, nor_1_out, not_5_out);
  and and_7 (and_7_out, comparator_20_eq, ISJUMP);
  assign controlled_buffer_4_out = and_7_out ? 21'h71f11 : 21'bz;  // Controlled_Buffer controlled_buffer_4
  and and_8 (and_8_out, not_2_out, comparator_20_eq);
  assign controlled_buffer_5_out = and_8_out ? 21'h76b30 : 21'bz;  // Controlled_Buffer controlled_buffer_5
  nor nor_2 (nor_2_out, comparator_22_eq, comparator_21_eq);
  assign controlled_buffer_6_out = nor_2_out ? 21'h76d54 : 21'bz;  // Controlled_Buffer controlled_buffer_6
  Pull_Resistor #(.pull(1)) pull_resistor_1 (.node(W_REG));
  and and_9 (and_9_out, ESTADO[1], comparator_2_eq);
  and and_10 (and_10_out, ESTADO[0], comparator_3_eq);
  and and_11 (and_11_out, ESTADO[2], comparator_4_eq);
  assign controlled_buffer_7_out = t0 ? 21'h76330 : 21'bz;  // Controlled_Buffer controlled_buffer_7
  assign controlled_buffer_8_out = t1 ? 21'h76d5c : 21'bz;  // Controlled_Buffer controlled_buffer_8
  assign controlled_buffer_9_out = t2 ? 21'h76f90 : 21'bz;  // Controlled_Buffer controlled_buffer_9
  and and_12 (and_12_out, or_2_out, comparator_7_eq);
  or or_3 (or_3_out, comparator_10_eq, comparator_11_eq, comparator_12_eq);
  assign controlled_buffer_10_out = t4 ? 21'h76d5c : 21'bz;  // Controlled_Buffer controlled_buffer_10
  or or_4 (or_4_out, comparator_13_eq, and_2_out);
  assign controlled_buffer_11_out = or_4_out ? 21'h76b30 : 21'bz;  // Controlled_Buffer controlled_buffer_11
  assign controlled_buffer_12_out = and_3_out ? EXECUTE : 21'bz;  // Controlled_Buffer controlled_buffer_12
  Pull_Resistor pull_resistor_2 (.node(pull_resistor_2_node));
  assign pull_resistor_2_node = comparator_15_eq ? EXECUTE : 21'bz;  // Controlled_Buffer controlled_buffer_13
  Pull_Resistor pull_resistor_3 (.node(controlled_buffer_3_out));
  assign controlled_buffer_14_out = and_5_out ? EXECUTE : 21'bz;  // Controlled_Buffer controlled_buffer_14
  Pull_Resistor pull_resistor_4 (.node(controlled_buffer_14_out));
  assign controlled_buffer_15_out = or_5_out ? 21'h76d54 : 21'bz;  // Controlled_Buffer controlled_buffer_15
  or or_5 (or_5_out, comparator_17_eq, and_6_out);
  and and_13 (and_13_out, comparator_18_eq, not_5_out);
  assign controlled_buffer_16_out = and_13_out ? 21'hf6c50 : 21'bz;  // Controlled_Buffer controlled_buffer_16
  and and_14 (and_14_out, comparator_19_eq, not_5_out);
  assign controlled_buffer_17_out = and_14_out ? 21'h76e50 : 21'bz;  // Controlled_Buffer controlled_buffer_17
  assign controlled_buffer_18_out = not_6_out ? EXECUTE : 21'bz;  // Controlled_Buffer controlled_buffer_18
  not not_6 (not_6_out, comparator_20_eq);
  assign controlled_buffer_19_out = comparator_21_eq ? 21'hf6c50 : 21'bz;  // Controlled_Buffer controlled_buffer_19
  Pull_Resistor pull_resistor_5 (.node(controlled_buffer_19_out));
  assign controlled_buffer_20_out = comparator_22_eq ? 21'h76e50 : 21'bz;  // Controlled_Buffer controlled_buffer_20
  Pull_Resistor pull_resistor_6 (.node(controlled_buffer_20_out));
  Pull_Resistor pull_resistor_7 (.node(controlled_buffer_6_out));
  Pull_Resistor pull_resistor_8 (.node(controlled_buffer_2_out));
  or or_6 (JUMP, comparator_1_eq, and_9_out, and_10_out, and_11_out);
  Multiplexer #(.select(4), .width(21)) multiplexer_2 (
    .in0(21'h76f11), .in1(21'h76c13), .in2(21'h17ef11), .in3(21'h18ef11), .in4(21'h1bef11), .in5(21'h1aef11),
    .in6(21'h1cef11), .in7(21'h19ef11), .in8(multiplexer_1_out), .in9(multiplexer_1_out),
    .in10(multiplexer_1_out), .in11(multiplexer_1_out), .in12(21'h77f13), .in13(21'h1def11),
    .in14(21'h1eef11), .in15(21'h76f00), .out(EXECUTE), .sel(\INSTRUÇÂO [7:4]));  // open: en
  or or_7 (or_7_out, and_1_out, and_12_out);
  assign controlled_buffer_21_out = and_15_out ? EXECUTE : 21'bz;  // Controlled_Buffer controlled_buffer_21
  and and_15 (and_15_out, or_3_out, t3);
  Pull_Resistor pull_resistor_9 (.node(controlled_buffer_11_out));
  Pull_Resistor pull_resistor_10 (.node(controlled_buffer_12_out));
  Pull_Resistor pull_resistor_11 (.node(controlled_buffer_15_out));
  Pull_Resistor pull_resistor_12 (.node(controlled_buffer_16_out));
  Pull_Resistor pull_resistor_13 (.node(controlled_buffer_17_out));
  Pull_Resistor pull_resistor_14 (.node(controlled_buffer_18_out));
  Pull_Resistor pull_resistor_15 (.node(controlled_buffer_4_out));
  Pull_Resistor pull_resistor_16 (.node(controlled_buffer_5_out));
  // Probe on EXECUTE
  Pull_Resistor pull_resistor_17 (.node(controlled_buffer_7_out));
  Pull_Resistor pull_resistor_18 (.node(controlled_buffer_8_out));
  Pull_Resistor pull_resistor_19 (.node(controlled_buffer_9_out));
  and and_16 (and_16_out, t3, comparator_8_eq);
  and and_17 (and_17_out, t3, comparator_9_eq);
  Pull_Resistor pull_resistor_20 (.node(controlled_buffer_10_out));
  assign controlled_buffer_22_out = and_16_out ? 21'h76f11 : 21'bz;  // Controlled_Buffer controlled_buffer_22
  assign controlled_buffer_23_out = and_17_out ? 21'h76f00 : 21'bz;  // Controlled_Buffer controlled_buffer_23
  assign or_8_out = controlled_buffer_11_out | controlled_buffer_12_out | pull_resistor_2_node | controlled_buffer_3_out | controlled_buffer_14_out;  // OR_Gate or_8, 21 bits wide
  assign controlled_buffer_24_out = t5 ? or_8_out : 21'bz;  // Controlled_Buffer controlled_buffer_24
  assign or_9_out = controlled_buffer_19_out | controlled_buffer_20_out | controlled_buffer_6_out;  // OR_Gate or_9, 21 bits wide
  Multiplexer #(.width(21)) multiplexer_3 (
    .in0(21'h76330), .in1(21'h76f19), .out(multiplexer_3_out), .sel(or_7_out));  // open: en
  Pull_Resistor pull_resistor_21 (.node(controlled_buffer_24_out));
  assign or_10_out = controlled_buffer_15_out | controlled_buffer_16_out | controlled_buffer_17_out;  // OR_Gate or_10, 21 bits wide
  assign controlled_buffer_25_out = t6 ? or_10_out : 21'bz;  // Controlled_Buffer controlled_buffer_25
  assign or_11_out = controlled_buffer_18_out | controlled_buffer_4_out | controlled_buffer_5_out;  // OR_Gate or_11, 21 bits wide
  assign controlled_buffer_26_out = t8 ? or_9_out : 21'bz;  // Controlled_Buffer controlled_buffer_26
  assign controlled_buffer_27_out = and_18_out ? multiplexer_3_out : 21'bz;  // Controlled_Buffer controlled_buffer_27
  and and_18 (and_18_out, t3, nor_3_out);
  nor nor_3 (nor_3_out, and_16_out, and_17_out, and_15_out);
  Pull_Resistor pull_resistor_22 (.node(controlled_buffer_25_out));
  assign controlled_buffer_28_out = t7 ? or_11_out : 21'bz;  // Controlled_Buffer controlled_buffer_28
  Pull_Resistor pull_resistor_23 (.node(controlled_buffer_28_out));
  Pull_Resistor pull_resistor_24 (.node(controlled_buffer_26_out));
  Pull_Resistor pull_resistor_25 (.node(controlled_buffer_27_out));
  Pull_Resistor pull_resistor_26 (.node(controlled_buffer_22_out));
  Pull_Resistor pull_resistor_27 (.node(controlled_buffer_23_out));
  Pull_Resistor pull_resistor_28 (.node(controlled_buffer_21_out));
  assign or_12_out = controlled_buffer_27_out | controlled_buffer_22_out | controlled_buffer_23_out | controlled_buffer_21_out;  // OR_Gate or_12, 21 bits wide
  assign {SAIDA, ULA, W_REG_CON, MUX_PC, W_PC, MUX_REM, MUX_RDM, W_RI, W_RDM, W_REM, ON, INC_PC, RM, WM, BREAK} = controlled_buffer_7_out | controlled_buffer_8_out | controlled_buffer_9_out | or_12_out | controlled_buffer_10_out | controlled_buffer_24_out | controlled_buffer_25_out | controlled_buffer_28_out | controlled_buffer_26_out | controlled_buffer_2_out;  // OR_Gate or_13, 21 bits wide

  assign MUX_X = \INSTRUÇÂO [3:2];

  // Other names for the same wires on the sheet: Z = ESTADO[0]; N = ESTADO[1]; C = ESTADO[2];
  //   OP[3:0] = \INSTRUÇÂO [7:4]; MODO[1:0] = \INSTRUÇÂO [1:0];
  //   SAIDA[18:0] = {ULA, W_REG_CON, MUX_PC, W_PC, MUX_REM, MUX_RDM, W_RI, W_RDM, W_REM, ON, INC_PC, RM, WM, BREAK};
  //   REG[1:0] = \INSTRUÇÂO [3:2]

  // Notes on the sheet:
  //   MODOS
  //   OPERAÇOES
  //   LOGICA DE DESVIO
  //   CONSTANTES
  //   MULTIPLEXADOR
  //   MICRO-INSTRUÇOES
  //   DECODIFICAÇAO
endmodule

module temp (
  input  [20:0] in_1,
  input  in_2,
  output [20:0] out_3
);

  Multiplexer #(.width(21)) multiplexer_1 (.in0(21'h76331), .in1(in_1), .out(out_3), .sel(in_2));  // open: en
endmodule

module Buffer_Duplamente_controlado (
  input  [20:0] in_1,
  input  in_2,
  input  in_3,
  output [20:0] out_4
);

  wire and_1_out;

  assign out_4 = and_1_out ? in_1 : 21'bz;  // Controlled_Buffer controlled_buffer_1
  Pull_Resistor pull_resistor_1 (.node(out_4));
  and and_1 (and_1_out, in_2, in_3);
endmodule

module MUX_3DIPLAY_7SEG (
  input  [7:0] Entrada,
  output [11:0] out_2,
  output [8:0] out_3
);

  wire [7:0] divider_1_out, divider_1_rem, divider_2_out, divider_2_rem;

  Divider divider_1 (.a(Entrada), .b(8'h64), .out(divider_1_out), .rem(divider_1_rem));  // open: upper
  Divider divider_2 (.a(divider_1_rem), .b(8'ha), .out(divider_2_out), .rem(divider_2_rem));  // open: upper
  MUX_DISPLAY_7SEG mux_display_7seg_1 (
    .a(divider_1_out[0]), .b(divider_1_out[1]), .c(divider_1_out[2]), .d(divider_1_out[3]), .x(out_2[0]),
    .y(out_2[1]), .z(out_2[2]), .u(out_2[3]), .v(out_3[0]), .w(out_3[1]), .s(out_3[2]));
  MUX_DISPLAY_7SEG mux_display_7seg_2 (
    .a(divider_2_out[0]), .b(divider_2_out[1]), .c(divider_2_out[2]), .d(divider_2_out[3]), .x(out_2[4]),
    .y(out_2[5]), .z(out_2[6]), .u(out_2[7]), .v(out_3[3]), .w(out_3[4]), .s(out_3[5]));
  MUX_DISPLAY_7SEG mux_display_7seg_3 (
    .a(divider_2_rem[0]), .b(divider_2_rem[1]), .c(divider_2_rem[2]), .d(divider_2_rem[3]), .x(out_2[8]),
    .y(out_2[9]), .z(out_2[10]), .u(out_2[11]), .v(out_3[6]), .w(out_3[7]), .s(out_3[8]));
endmodule

module MUX_DISPLAY_7SEG (
  input  a,
  input  b,
  input  c,
  input  d,
  output x,
  output y,
  output z,
  output u,
  output v,
  output w,
  output s
);

  wire and_1_out, and_2_out, and_3_out, and_4_out, and_5_out, and_6_out, and_7_out, and_8_out, and_9_out,
       and_10_out, and_11_out, and_12_out, and_13_out, and_14_out, and_15_out, and_16_out, and_17_out,
       and_18_out, and_19_out, and_20_out, and_21_out, and_22_out, and_23_out, and_24_out, and_25_out,
       and_26_out, and_27_out, and_28_out, and_29_out, and_30_out, and_31_out, and_32_out, not_1_out,
       not_2_out, not_3_out, not_4_out, not_5_out, not_6_out, not_7_out, not_8_out, not_9_out, not_10_out,
       not_11_out, not_12_out, not_13_out, not_14_out, not_15_out, not_16_out, not_17_out, not_18_out,
       not_19_out, not_20_out, not_21_out, not_22_out, not_23_out, not_24_out, not_25_out, not_26_out,
       not_27_out, not_28_out, not_29_out, not_30_out, not_31_out, not_32_out, not_33_out, not_34_out,
       not_35_out, not_36_out, not_37_out, not_38_out, not_39_out, not_40_out;

  not not_1 (not_1_out, b);
  and and_1 (and_1_out, not_1_out, not_2_out, d);
  not not_2 (not_2_out, c);
  not not_3 (not_3_out, b);
  and and_2 (and_2_out, not_3_out, c, not_4_out);
  not not_4 (not_4_out, d);
  not not_5 (not_5_out, a);
  and and_3 (and_3_out, not_5_out, b, not_6_out);
  not not_6 (not_6_out, d);
  and and_4 (and_4_out, b, not_7_out, not_8_out);
  not not_7 (not_7_out, c);
  not not_8 (not_8_out, d);
  not not_9 (not_9_out, a);
  and and_5 (and_5_out, not_9_out, not_10_out);
  not not_10 (not_10_out, b);
  not not_11 (not_11_out, a);
  and and_6 (and_6_out, not_11_out, c);
  not not_12 (not_12_out, b);
  and and_7 (and_7_out, not_12_out, c);
  and and_8 (and_8_out, a, d);
  not not_13 (not_13_out, a);
  and and_9 (and_9_out, not_13_out, not_14_out, not_15_out);
  not not_14 (not_14_out, b);
  not not_15 (not_15_out, c);
  not not_16 (not_16_out, b);
  and and_10 (and_10_out, not_16_out, d);
  and and_11 (and_11_out, b, not_17_out);
  not not_17 (not_17_out, d);
  and and_12 (and_12_out, b, c);
  and and_13 (and_13_out, a, d);
  and and_14 (and_14_out, a, c);
  not not_18 (not_18_out, a);
  and and_15 (and_15_out, not_18_out, not_19_out);
  not not_19 (not_19_out, b);
  not not_20 (not_20_out, b);
  and and_16 (and_16_out, not_20_out, not_21_out);
  not not_21 (not_21_out, c);
  not not_22 (not_22_out, c);
  and and_17 (and_17_out, not_22_out, not_23_out);
  not not_23 (not_23_out, d);
  and and_18 (and_18_out, c, d);
  and and_19 (and_19_out, a, b);
  not not_24 (not_24_out, a);
  and and_20 (and_20_out, not_24_out, not_25_out, not_26_out);
  not not_25 (not_25_out, b);
  not not_26 (not_26_out, c);
  and and_21 (and_21_out, c, d);
  not not_27 (not_27_out, a);
  and and_22 (and_22_out, not_27_out, b, not_28_out);
  not not_28 (not_28_out, d);
  and and_23 (and_23_out, a, b, d);
  not not_29 (not_29_out, a);
  and and_24 (and_24_out, not_29_out, not_30_out, not_31_out);
  not not_30 (not_30_out, c);
  not not_31 (not_31_out, d);
  not not_32 (not_32_out, b);
  and and_25 (and_25_out, not_32_out, d);
  and and_26 (and_26_out, c, d);
  not not_33 (not_33_out, a);
  and and_27 (and_27_out, not_33_out, b, not_34_out);
  not not_34 (not_34_out, d);
  not not_35 (not_35_out, b);
  and and_28 (and_28_out, a, not_35_out, c);
  and and_29 (and_29_out, a, b, not_36_out);
  not not_36 (not_36_out, c);
  not not_37 (not_37_out, b);
  and and_30 (and_30_out, not_37_out, not_38_out);
  not not_38 (not_38_out, c);
  and and_31 (and_31_out, c, not_39_out);
  not not_39 (not_39_out, d);
  and and_32 (and_32_out, a, not_40_out);
  not not_40 (not_40_out, c);
  or or_1 (x, and_1_out, and_2_out, and_3_out, and_4_out);
  or or_2 (y, and_5_out, and_6_out, and_7_out, and_8_out);
  or or_3 (u, and_15_out, and_16_out, and_17_out, and_18_out, and_19_out);
  or or_4 (v, and_20_out, and_21_out, and_22_out, and_23_out);
  or or_5 (s, and_30_out, and_31_out, and_32_out);
  or or_6 (z, and_9_out, and_10_out, and_11_out, and_12_out, and_13_out, and_14_out);
  or or_7 (w, and_24_out, and_25_out, and_26_out, and_27_out, and_28_out, and_29_out);
endmodule
